// Logisim project Abterra I.circ as structural Verilog: 6 circuits, main circuit Main
module ALU (
  input  ADD,
  input  NOT,
  input  AND,
  input  NEG,
  input  [10:0] acc,
  input  [10:0] ram,
  output [10:0] out
);

  wire [10:0] adder_1_out, and_1_out, negator_1_out, not_1_out;

  assign out = ADD ? adder_1_out : 11'bz;  // Controlled_Buffer controlled_buffer_1
  Adder #(.width(11)) adder_1 (.a(acc), .b(ram), .out(adder_1_out));  // open: cin, cout
  Negator #(.width(11)) negator_1 (.in(ram), .out(negator_1_out));
  assign out = NEG ? negator_1_out : 11'bz;  // Controlled_Buffer controlled_buffer_2
  assign out = AND ? and_1_out : 11'bz;  // Controlled_Buffer controlled_buffer_3
  assign and_1_out = acc & ram;  // AND_Gate and_1, 11 bits wide
  assign not_1_out = ~ram;  // NOT_Gate not_1, 11 bits wide
  assign out = NOT ? not_1_out : 11'bz;  // Controlled_Buffer controlled_buffer_4
endmodule

module Zero_tester (
  input  [10:0] value,
  output zero
);

  wire or_1_out;

  or or_1 (or_1_out, value[0], value[1], value[2], value[3], value[4], value[5], value[6], value[7], value[8], value[9], value[10]);
  not not_1 (zero, or_1_out);
endmodule

module BIT_test (
  input  [3:0] select,
  input  [10:0] Value,
  output out
);

  Multiplexer #(.select(4), .enable("false")) multiplexer_1 (
    .in0(Value[0]), .in1(Value[1]), .in2(Value[2]), .in3(Value[3]), .in4(Value[4]), .in5(Value[5]),
    .in6(Value[6]), .in7(Value[7]), .in8(Value[8]), .in9(Value[9]), .in10(Value[10]), .in11(1'b0),
    .in12(1'b0), .in13(1'b0), .in14(1'b0), .in15(1'b0), .out(out), .sel(select));
endmodule

module Main (
  input  Disable_breakpoint,
  input  Disable_breakpoint_2
);

  wire alu_redesign_1_carry, and_1_out, and_3_out, and_4_out, and_5_out, and_6_out, and_7_out, and_8_out,
       bit_test_1_out, clock_1_out, control_unit_1__0__alub_ramb, control_unit_1__1__en_pc,
       control_unit_1__2__in1_acc, control_unit_1__3__in1_pc, control_unit_1__4__not, control_unit_1__5_and,
       control_unit_1__6_add, control_unit_1__7_en_acc, control_unit_1__8_neg, control_unit_1__9_in2_ram,
       control_unit_1__10_in2_cu, control_unit_1__11_addr_pc, control_unit_1__14_jmp,
       control_unit_1__14_skip, control_unit_1__16_ld, control_unit_1__17_alub_alu,
       control_unit_1__18_en_ram, control_unit_1__19_addr__instr, control_unit_1__20_en_ir,
       control_unit_1__21_alub_jump_to, fetch_ex_q, jmp_q, not_1_out, not_2_out, not_3_out, or_1_out,
       or_2_out, or_3_out, or_4_out, register_1_q, register_2_q, reset_out, skip_q, zero_tester_1_zero;
  wire [1:0] and_2_out, control_unit_1__12_13_too_in2;
  wire [1:1] begin_q;
  wire [2:0] IR_q_2;
  wire [7:0] controlled_buffer_3_out, controlled_buffer_6_out, IR_q, jmp_too_q, xnor_1_out;
  wire [10:0] acc_q, alu_redesign_1_out, controlled_buffer_1_out, controlled_buffer_4_out, PC_q, ram_1_data,
       xnor_2_out;
  wire [10:8] controlled_buffer_3_out_2, controlled_buffer_7_out;

  Register #(.width(1)) register_1 (
    .D(alu_redesign_1_carry), .Q(register_1_q), .clk(register_2_q), .clr(reset_out));  // open: en
  and and_1 (and_1_out, control_unit_1__6_add, fetch_ex_q);
  ALU_redesign alu_redesign_1 (
    .acc(controlled_buffer_1_out), .ram(controlled_buffer_4_out), .out(alu_redesign_1_out),
    .ADD(control_unit_1__6_add), .NOT(control_unit_1__4__not), .AND(control_unit_1__5_and),
    .NEG(control_unit_1__8_neg), .carry(alu_redesign_1_carry));
  assign controlled_buffer_1_out = control_unit_1__2__in1_acc ? acc_q : 11'bz;  // Controlled_Buffer controlled_buffer_1
  assign controlled_buffer_1_out = control_unit_1__3__in1_pc ? PC_q : 11'bz;  // Controlled_Buffer controlled_buffer_2
  Zero_tester zero_tester_1 (.value(acc_q), .zero(zero_tester_1_zero));
  assign {controlled_buffer_3_out_2, controlled_buffer_3_out} = control_unit_1__17_alub_alu ? alu_redesign_1_out : 11'bz;  // Controlled_Buffer controlled_buffer_3
  assign controlled_buffer_4_out = control_unit_1__9_in2_ram ? ram_1_data : 11'bz;  // Controlled_Buffer controlled_buffer_4
  assign controlled_buffer_4_out = control_unit_1__10_in2_cu ? {{9{1'b0}}, and_2_out} : 11'bz;  // Controlled_Buffer controlled_buffer_5
  Register #(.width(11)) acc (
    .D({controlled_buffer_3_out_2, controlled_buffer_3_out}), .en(control_unit_1__7_en_acc), .Q(acc_q),
    .clk(register_2_q), .clr(reset_out));
  BIT_test bit_test_1 (.Value(acc_q), .out(bit_test_1_out), .select(IR_q[7:4]));
  Register PC (
    .D(controlled_buffer_3_out), .en(control_unit_1__1__en_pc), .Q(PC_q[7:0]), .clk(register_2_q),
    .clr(reset_out));
  not not_1 (not_1_out, control_unit_1__16_ld);
  assign controlled_buffer_6_out = control_unit_1__19_addr__instr ? IR_q : 8'bz;  // Controlled_Buffer controlled_buffer_6
  assign {controlled_buffer_7_out, controlled_buffer_6_out} = control_unit_1__11_addr_pc ? PC_q : 11'bz;  // Controlled_Buffer controlled_buffer_7
  assign and_2_out = control_unit_1__12_13_too_in2 & {2{begin_q[1]}};  // AND_Gate and_2, 2 bits wide
  RAM #(.dataWidth(11), .bus("separate")) ram_1 (
    .addr(controlled_buffer_6_out), .din(acc_q), .data(ram_1_data), .str(not_1_out),
    .sel(control_unit_1__18_en_ram), .clk(register_2_q), .ld(control_unit_1__16_ld));  // open: clr
  assign controlled_buffer_3_out = control_unit_1__21_alub_jump_to ? jmp_too_q : 8'bz;  // Controlled_Buffer controlled_buffer_8
  assign {controlled_buffer_3_out_2, controlled_buffer_3_out} = control_unit_1__0__alub_ramb ? ram_1_data : 11'bz;  // Controlled_Buffer controlled_buffer_9
  Register #(.width(11), .trigger("high")) IR (
    .D(ram_1_data), .en(control_unit_1__20_en_ir), .Q({IR_q_2, IR_q}), .clk(register_2_q), .clr(reset_out));
  Clock clock_1 (.out(clock_1_out));
  and and_3 (and_3_out, xnor_1_out[0], xnor_1_out[1], xnor_1_out[2], xnor_1_out[3], xnor_1_out[4], xnor_1_out[5], xnor_1_out[6], xnor_1_out[7]);
  or or_1 (or_1_out, register_2_q, not_2_out);
  not not_2 (not_2_out, begin_q[1]);
  Register #(.width(1), .trigger("falling")) fetch_ex (
    .D(not_3_out), .Q(fetch_ex_q), .clk(register_2_q), .clr(reset_out));  // open: en
  not not_3 (not_3_out, fetch_ex_q);
  Control_unit control_unit_1 (
    ._14_jmp(control_unit_1__14_jmp), .skip(skip_q), .JMP(jmp_q), ._14_skip(control_unit_1__14_skip),
    ._21_ALUb_JUMP_to(control_unit_1__21_alub_jump_to), ._20_en_IR(control_unit_1__20_en_ir),
    ._19_addr__instr(control_unit_1__19_addr__instr), ._18_en_RAM(control_unit_1__18_en_ram), .instr(IR_q_2),
    ._17_ALUb_ALU(control_unit_1__17_alub_alu), ._16_ld(control_unit_1__16_ld), .fetch_ex(fetch_ex_q),
    ._0__ALUb_Ramb(control_unit_1__0__alub_ramb), ._1__en_PC(control_unit_1__1__en_pc),
    ._2__in1_acc(control_unit_1__2__in1_acc), ._3__in1_PC(control_unit_1__3__in1_pc),
    ._4__NOT(control_unit_1__4__not), ._5_AND(control_unit_1__5_and), ._6_ADD(control_unit_1__6_add),
    ._7_en_acc(control_unit_1__7_en_acc), ._8_NEG(control_unit_1__8_neg),
    ._9_in2_ram(control_unit_1__9_in2_ram), ._10_in2_cu(control_unit_1__10_in2_cu),
    ._11_addr_PC(control_unit_1__11_addr_pc), ._12_13_too_in2(control_unit_1__12_13_too_in2));
  and and_4 (and_4_out, or_4_out, or_2_out);
  Register #(.width(1), .trigger("high")) register_2 (
    .D(clock_1_out), .Q(register_2_q), .clk(and_4_out), .clr(reset_out));  // open: en
  Register #(.width(1), .trigger("falling")) \begin  (
    .D(1'b1), .Q(begin_q[1]), .clk(register_2_q), .clr(reset_out));  // open: en
  Register #(.width(1), .trigger("high")) skip (
    .D(or_3_out), .Q(skip_q), .clk(register_2_q), .clr(reset_out));  // open: en
  assign xnor_1_out = ~(8'h24 ^ PC_q[7:0]);  // XNOR_Gate xnor_1, 8 bits wide
  Register #(.width(1)) jmp (.D(control_unit_1__14_jmp), .Q(jmp_q), .clk(register_2_q), .clr(reset_out));  // open: en
  or or_2 (or_2_out, Disable_breakpoint, ~and_3_out);  // OR_Gate
  or or_3 (or_3_out, and_6_out, and_8_out, and_5_out);
  Register #(.trigger("high")) jmp_too (
    .D(IR_q), .en(control_unit_1__14_jmp), .Q(jmp_too_q), .clk(register_2_q), .clr(reset_out));
  and and_5 (and_5_out, IR_q[1], bit_test_1_out, control_unit_1__14_skip);
  and and_6 (and_6_out, IR_q[3], zero_tester_1_zero, control_unit_1__14_skip);
  Button reset (.out(reset_out));
  and and_7 (and_7_out, xnor_2_out[0], xnor_2_out[1], xnor_2_out[2], xnor_2_out[3], xnor_2_out[4], xnor_2_out[5], xnor_2_out[6], xnor_2_out[7], xnor_2_out[8], xnor_2_out[9], xnor_2_out[10]);
  and and_8 (and_8_out, IR_q[2], register_1_q, control_unit_1__14_skip);
  or or_4 (or_4_out, Disable_breakpoint_2, ~and_7_out);  // OR_Gate
  assign xnor_2_out = ~(11'h140 ^ {IR_q_2, IR_q});  // XNOR_Gate xnor_2, 11 bits wide
endmodule

module ALU_redesign (
  input  ADD,
  input  NOT,
  input  AND,
  input  NEG,
  input  [10:0] acc,
  input  [10:0] ram,
  output [10:0] out,
  output carry
);

  wire [10:0] adder_1_out, and_1_out, negator_1_out, not_1_out;

  assign out = ADD ? adder_1_out : 11'bz;  // Controlled_Buffer controlled_buffer_1
  Adder #(.width(11)) adder_1 (.a(acc), .b(ram), .out(adder_1_out), .cout(carry));  // open: cin
  assign out = NEG ? negator_1_out : 11'bz;  // Controlled_Buffer controlled_buffer_2
  Negator #(.width(11)) negator_1 (.in(ram), .out(negator_1_out));
  assign out = AND ? and_1_out : 11'bz;  // Controlled_Buffer controlled_buffer_3
  assign and_1_out = acc & ram;  // AND_Gate and_1, 11 bits wide
  assign not_1_out = ~ram;  // NOT_Gate not_1, 11 bits wide
  assign out = NOT ? not_1_out : 11'bz;  // Controlled_Buffer controlled_buffer_4
endmodule

module Control_unit (
  input  fetch_ex,
  input  [2:0] instr,
  input  skip,
  input  JMP,
  output _20_en_IR,
  output _19_addr__instr,
  output _18_en_RAM,
  output _17_ALUb_ALU,
  output _16_ld,
  output _21_ALUb_JUMP_to,
  output _14_jmp,
  output _14_skip,
  output _0__ALUb_Ramb,
  output _1__en_PC,
  output _2__in1_acc,
  output _3__in1_PC,
  output _4__NOT,
  output _5_AND,
  output _6_ADD,
  output _7_en_acc,
  output _8_NEG,
  output _9_in2_ram,
  output _10_in2_cu,
  output _11_addr_PC,
  output [1:0] _12_13_too_in2
);

  wire nor_1_out, not_1_out;
  wire [21:0] controlled_buffer_1_out;

  not not_1 (not_1_out, fetch_ex);
  nor nor_1 (nor_1_out, skip, JMP);
  assign controlled_buffer_1_out = nor_1_out ? 22'h171c4a : 22'bz;  // Controlled_Buffer controlled_buffer_1
  assign controlled_buffer_1_out = JMP ? 22'h350802 : 22'bz;  // Controlled_Buffer controlled_buffer_2
  assign controlled_buffer_1_out = skip ? 22'h172c4a : 22'bz;  // Controlled_Buffer controlled_buffer_3
  ROM #(.addrWidth(3), .dataWidth(22)) rom_1 (
    .addr(instr),
    .data({_21_ALUb_JUMP_to, _20_en_IR, _19_addr__instr, _18_en_RAM, _17_ALUb_ALU, _16_ld, _14_jmp, _14_skip, _12_13_too_in2, _11_addr_PC, _10_in2_cu, _9_in2_ram, _8_NEG, _7_en_acc, _6_ADD, _5_AND, _4__NOT, _3__in1_PC, _2__in1_acc, _1__en_PC, _0__ALUb_Ramb}),
    .sel(fetch_ex));
  assign {_21_ALUb_JUMP_to, _20_en_IR, _19_addr__instr, _18_en_RAM, _17_ALUb_ALU, _16_ld, _14_jmp, _14_skip, _12_13_too_in2, _11_addr_PC, _10_in2_cu, _9_in2_ram, _8_NEG, _7_en_acc, _6_ADD, _5_AND, _4__NOT, _3__in1_PC, _2__in1_acc, _1__en_PC, _0__ALUb_Ramb} = not_1_out ? controlled_buffer_1_out : 22'bz;  // Controlled_Buffer controlled_buffer_4

  // Notes on the sheet:
  //   contents of rom_1 (hex, n*v repeats v):
  //   d0081 c0000 f02a4 f0290 f02c4 f0380 4000 8000
endmodule
